# Fritzing sketch water_meter (saved by Fritzing 0.9.5d)
circuit board: 10cm x 6cm
breadboards: 1

parts:
  A1 = Esp32-c3 super mini
  A2 = lcd color display 1.3in 240x240 7pin interface [package=THT]
  HC-SR04_Sensor_1 = HC-SR04 Ultrasonic Distance Sensor

nets:
  N1: A1.Pin_2, A2.SDA
  N2: A1.Pin_6, A2.BLK
  N3: A1.Pin_9, HC-SR04_Sensor_1.TRIG
  N4: A1.Pin_10, HC-SR04_Sensor_1.ECHO
  N5: A1.Pin_11, A2.DC
  N6: A1.Pin_12, A2.RES
  N7: A1.Pin_13, A2.SCL
  N8: A1.Pin_14, A2.VCC
  GND: A1.Pin_15, A2.GND, HC-SR04_Sensor_1.GND
  N9: A1.Pin_16, HC-SR04_Sensor_1.VCC

custom parts:
  Esp32-c3 super mini: ESP32-C3 Development Board ESP32 SuperMini Development Board ESP32 Development Board WiFi Bluetooth.
  lcd color display 1.3in 240x240 7pin interface: 1.3 Inch Color 240 x 240 IPS TFT LCD Display Screen Module Board 7 Pin 4 Wire ST7789VW Drive IC SPI interface.
